# Fritzing sketch magsensor (saved by Fritzing 0.9.2b)
breadboards: 1

parts:
  U1 = RF-LINK_TX [package=rf-link_tx]
  Magnetic_Switch = SWITCH-MOMENTARY-2 [package=tactile-pth]
  R1 = Resistor [tolerance=±5% resistance=10k package="2010 [SMD]"]
  U2 = atmega328 [package=dip]
  R2 = Resistor [tolerance=±5% resistance=220 package="2010 [SMD]"]
  R3 = Resistor [tolerance=±5% resistance=10k package="2010 [SMD]"]
  R1_2 = Resistor [tolerance=±5% resistance=10k package="2010 [SMD]"]
  Diag_switch = SWITCH-MOMENTARY-2 [package=reed_switch_pth]
  C1 = Capacitor [package=0402-cap]
  LED1 = smd LED [color="Red (633nm)" package="0603 [SMD]"]
  J1 = female pin header, 2 pins [form="♀ (female)"]

nets:
  N1: U1.DATA, U2.D10_(PWM)
  GND: U1.GND, R1.Pin_1, U2.GND, R2.Pin_1, R3.Pin_1, C1.1
  N2: U1.+5V, U2.D13
  5V: Magnetic_Switch.1, U2.VCC, U2.AVCC, U2.AREF, R1_2.Pin_0, Diag_switch.2
  N3: Magnetic_Switch.2, R1.Pin_0, U2.D2
  N4: U2.RESET, R1_2.Pin_1, C1.2
  N5: U2.D0_(RX), J1.pin2
  N6: U2.D1_(TX), J1.pin1
  N7: U2.D3_(PWM), R3.Pin_0, Diag_switch.1
  N8: U2.D9_(PWM), LED1.anode
  N9: R2.Pin_0, LED1.cathode

notes:
  WARNING : Atmega pins are used as in real live. Meaning, pin 15 (D9) is actually pin 28 and pin 28 (A5) in pin 15.
